# Fritzing sketch KTerMR1 (saved by Fritzing 0.9.3b)
circuit board: 8.46667cm x 5.64444cm
breadboards: 1

parts:
  328_MCU = atmega328 [package=dip]
  +_- = Battery
  C1 = Electrolytic Capacitor [capacitance=1µF package="100 mil [THT, electrolytic]"]
  C2 = Electrolytic Capacitor [capacitance=1µF package="100 mil [THT, electrolytic]"]
  R1 = Resistor [tolerance=±5% resistance=220 package=THT]
  LED1 = LED - 5mm [color="Red (633nm)" package="5 mm [THT]"]
  U1 = Voltage Regulator - 3.3V [package="TO220 [THT]"]
  CLK = female pin header, 1 pin [form="♀ (female)"]
  R2 = Resistor [tolerance=±5% resistance=220 package=THT]
  RX = female pin header, 1 pin [form="♀ (female)"]
  TX = female pin header, 1 pin [form="♀ (female)"]
  D2 = female pin header, 1 pin [form="♀ (female)"]
  D3 = female pin header, 1 pin [form="♀ (female)"]
  D4 = female pin header, 1 pin [form="♀ (female)"]
  XTAL1 = Crystal [frequency="16 Mhz" package=THT]
  C3 = Ceramic Capacitor [capacitance=100nF package="200 mil [THT, multilayer]"]
  C4 = Ceramic Capacitor [capacitance=100nF package="200 mil [THT, multilayer]"]
  LED2 = RGB LED (com. cathode, rgb) [package="5 mm [THT]"]
  R3 = Resistor [tolerance=±5% resistance=220 package=THT]
  R4 = Resistor [tolerance=±5% resistance=220 package=THT]
  R5 = Resistor [tolerance=±5% resistance=220 package=THT]
  D5 = female pin header, 1 pin [form="♀ (female)"]
  A5 = female pin header, 1 pin [form="♀ (female)"]
  A4 = female pin header, 1 pin [form="♀ (female)"]
  A3 = female pin header, 1 pin [form="♀ (female)"]
  A2 = female pin header, 1 pin [form="♀ (female)"]
  A1 = female pin header, 1 pin [form="♀ (female)"]
  A0 = female pin header, 1 pin [form="♀ (female)"]
  R6 = Resistor [tolerance=±5% resistance=220 package=THT]
  LED3 = LED - 5mm [color="Red (633nm)" package="5 mm [THT]"]
  AREF = female pin header, 1 pin [form="♀ (female)"]
  D12 = female pin header, 1 pin [form="♀ (female)"]
  11 = female pin header, 1 pin [form="♀ (female)"]
  10 = female pin header, 1 pin [form="♀ (female)"]
  9 = female pin header, 1 pin [form="♀ (female)"]
  COUT = female pin header, 1 pin [form="♀ (female)"]

nets:
  N1: 328_MCU.RESET, CLK.pin1, R2.Pin_0
  N2: 328_MCU.D0_(RX), RX.pin1
  N3: 328_MCU.D1_(TX), TX.pin1
  N4: 328_MCU.D2, D2.pin1
  N5: 328_MCU.D3_(PWM), D3.pin1
  N6: 328_MCU.D4, D4.pin1
  N7: 328_MCU.VCC, 328_MCU.AVCC, C2.+, R1.Pin_1, U1.output_voltage, R2.Pin_1
  GND: 328_MCU.GND, +_-.-, C1.-, C2.-, LED1.anode, U1.GND, C3.0, C4.0, LED2.common_cathode, R6.Pin_0
  N8: 328_MCU.XLAT1, XTAL1.pin_0, C3.1
  N9: 328_MCU.XLAT2, XTAL1.pin_1, C4.1
  N10: 328_MCU.D5_(PWM), D5.pin1
  N11: 328_MCU.D6_(PWM), R5.Pin_0
  N12: 328_MCU.D7, R4.Pin_0
  N13: 328_MCU.D8, R3.Pin_0
  N14: 328_MCU.D9_(PWM), 9.pin1
  N15: 328_MCU.D10_(PWM), 10.pin1
  N16: 328_MCU.D11_(PWM), 11.pin1
  N17: 328_MCU.D12, D12.pin1
  N18: 328_MCU.D13, LED3.cathode, COUT.pin1
  N19: 328_MCU.AREF, AREF.pin1
  N20: 328_MCU.A0, A0.pin1
  N21: 328_MCU.A1, A1.pin1
  N22: 328_MCU.A2, A2.pin1
  N23: 328_MCU.A3, A3.pin1
  N24: 328_MCU.A4, A4.pin1
  N25: 328_MCU.A5, A5.pin1
  N26: +_-.+, C1.+, U1.input_voltage
  N27: R1.Pin_0, LED1.cathode
  N28: LED2.red_anode, R5.Pin_1
  N29: LED2.green_anode, R4.Pin_1
  N30: LED2.blue_anode, R3.Pin_1
  N31: R6.Pin_1, LED3.anode

notes:
  KTerM
  R1
